// Logisim project PX16C.circ as structural Verilog: 1 circuit, main circuit main
module main (
);

  wire AADD, adder_1_cout, AIA, AIB, and_1_out, and_2_p2, and_3_out, and_4_out, and_5_p4, and_6_out,
       and_7_p5, and_7_p6, and_9_p2, and_10_p2, and_10_p3, AOR, ASHL, ASHR, AXB, AXOR, Cin, CLK,
       comparator_1_lt, Cout, decoder_1_out0, decoder_1_out1, decoder_1_out2, decoder_1_out3, decoder_1_out4,
       decoder_1_out5, decoder_1_out6, decoder_2_out0, decoder_2_out1, decoder_2_out2, decoder_2_out3,
       decoder_2_out4, decoder_2_out5, decoder_2_out6, decoder_2_out7, decoder_3_out0, decoder_3_out1,
       decoder_3_out2, decoder_3_out3, decoder_3_out4, decoder_3_out5, decoder_3_out6, decoder_3_out7,
       decoder_4_out0, decoder_4_out1, decoder_4_out2, decoder_4_out4, demultiplexer_1_out0,
       demultiplexer_1_out1, demultiplexer_2_out0, demultiplexer_2_out1, demultiplexer_3_out0,
       demultiplexer_3_out1, demultiplexer_4_out1, demultiplexer_5_out1, demultiplexer_6_out1,
       demultiplexer_7_out0, demultiplexer_7_out1, demultiplexer_8_out0, demultiplexer_8_out1,
       demultiplexer_9_out1, demultiplexer_10_out0, demultiplexer_10_out1, INC, IY, multiplexer_2_out,
       nand_1_out, nand_2_out, nand_3_out, nor_1_out, nor_2_p2, not_1_out, not_2_out, not_3_out, not_5_out,
       not_6_out, not_7_out, not_9_out, or_2_p5, or_3_p2, or_5_out, or_7_out, or_13_p3, or_19_p2, or_20_p2,
       or_21_out, R4, R6, RM, RST, SCout, Si0, Si1, WM, WR, xor_7_p3;
  wire [2:0] A, B, D, IA, IB, IX, multiplexer_3_out, multiplexer_4_out, multiplexer_5_out;
  wire [2:2] or_18_out;
  wire [5:0] IOp;
  wire [9:0] PS;
  wire [9:1] not_4_out;
  wire [15:0] Ab, adder_1_out, AR_q, bit_extender_1_out, bit_extender_2_out, bit_extender_3_out,
       controlled_buffer_17_out, controlled_buffer_18_out, Db, imm0_q, imm1_q, or_1_p3, PbA, PbB, PC_q, PF_q,
       R0_q, R1_q, R2_q, R3_q, ram_1_data, Rb, rom_1_data, ST_q, xor_1_out, xor_2_out, xor_3_out, xor_4_out,
       xor_5_out, xor_6_out;

  // Probe on PbA
  DotMatrix #(.inputtype("row"), .matrixcols(8), .matrixrows(2), .dotshape("circle")) dotmatrix_1 (
    .row0(PbA[15:8]), .row1(PbA[7:0]));
  // Probe on PbB
  DotMatrix #(.inputtype("row"), .matrixcols(8), .matrixrows(2), .dotshape("circle")) dotmatrix_2 (
    .row0(PbB[15:8]), .row1(PbB[7:0]));
  // Probe on Rb
  DotMatrix #(.inputtype("row"), .matrixcols(8), .matrixrows(2), .dotshape("circle")) dotmatrix_3 (
    .row0(Rb[15:8]), .row1(Rb[7:0]));
  // Probe on Db
  DotMatrix #(.inputtype("row"), .matrixcols(8), .matrixrows(2), .dotshape("circle")) dotmatrix_4 (
    .row0(Db[15:8]), .row1(Db[7:0]));
  // Probe on Ab
  DotMatrix #(.inputtype("row"), .matrixcols(8), .matrixrows(2), .dotshape("circle")) dotmatrix_5 (
    .row0(Ab[15:8]), .row1(Ab[7:0]));
  // Probe on PbA
  // Probe on PbB
  // Probe on Rb
  // Probe on Db
  // Probe on Ab
  Button button_1 (.out(RST));
  Clock clock_1 (.out(CLK));
  Decoder #(.select(3), .disabled(0), .enable("true")) decoder_1 (
    .out0(decoder_1_out0), .out1(decoder_1_out1), .out2(decoder_1_out2), .out3(decoder_1_out3),
    .out4(decoder_1_out4), .out5(decoder_1_out5), .out6(decoder_1_out6), .out7(WM), .sel(D), .en(WR));
  Register #(.width(16)) R0 (.D(Db), .en(decoder_1_out0), .Q(R0_q), .clk(CLK), .clr(RST));
  Register #(.width(16)) R1 (.D(Db), .en(decoder_1_out1), .Q(R1_q), .clk(CLK), .clr(RST));
  Register #(.width(16)) R2 (.D(Db), .en(decoder_1_out2), .Q(R2_q), .clk(CLK), .clr(RST));
  Register #(.width(16)) R3 (.D(Db), .en(decoder_1_out3), .Q(R3_q), .clk(CLK), .clr(RST));
  Register #(.width(16)) ST (.D(Db), .en(decoder_1_out4), .Q(ST_q), .clk(CLK), .clr(RST));
  Register #(.width(16)) PF (.D(Db), .en(decoder_1_out5), .Q(PF_q), .clk(CLK), .clr(RST));
  Counter #(.width(16), .max('hffff)) PC (
    .load(decoder_1_out6), .D(Db), .count(INC), .Q(PC_q), .clk(CLK), .clr(RST));  // open: carry
  Register #(.width(16)) imm0 (.D(Db), .en(Si0), .Q(imm0_q), .clk(CLK), .clr(RST));
  Register #(.width(16)) imm1 (.D(Db), .en(Si1), .Q(imm1_q), .clk(CLK), .clr(RST));
  assign PbA = decoder_2_out0 ? R0_q : 16'bz;  // Controlled_Buffer controlled_buffer_1
  assign PbB = decoder_3_out0 ? R0_q : 16'bz;  // Controlled_Buffer controlled_buffer_2
  assign PbA = decoder_2_out1 ? R1_q : 16'bz;  // Controlled_Buffer controlled_buffer_3
  assign PbB = decoder_3_out1 ? R1_q : 16'bz;  // Controlled_Buffer controlled_buffer_4
  assign PbA = decoder_2_out2 ? R2_q : 16'bz;  // Controlled_Buffer controlled_buffer_5
  assign PbB = decoder_3_out2 ? R2_q : 16'bz;  // Controlled_Buffer controlled_buffer_6
  assign PbA = decoder_2_out3 ? R3_q : 16'bz;  // Controlled_Buffer controlled_buffer_7
  assign PbB = decoder_3_out3 ? R3_q : 16'bz;  // Controlled_Buffer controlled_buffer_8
  assign PbA = decoder_2_out4 ? ST_q : 16'bz;  // Controlled_Buffer controlled_buffer_9
  assign PbB = decoder_3_out4 ? ST_q : 16'bz;  // Controlled_Buffer controlled_buffer_10
  assign PbA = decoder_2_out5 ? PF_q : 16'bz;  // Controlled_Buffer controlled_buffer_11
  assign PbB = decoder_3_out5 ? PF_q : 16'bz;  // Controlled_Buffer controlled_buffer_12
  assign PbA = decoder_2_out6 ? PC_q : 16'bz;  // Controlled_Buffer controlled_buffer_13
  assign PbB = decoder_3_out6 ? PC_q : 16'bz;  // Controlled_Buffer controlled_buffer_14
  assign PbA = decoder_2_out7 ? imm0_q : 16'bz;  // Controlled_Buffer controlled_buffer_15
  assign PbB = decoder_3_out7 ? imm1_q : 16'bz;  // Controlled_Buffer controlled_buffer_16
  Decoder #(.select(3), .disabled(0)) decoder_2 (
    .out0(decoder_2_out0), .out1(decoder_2_out1), .out2(decoder_2_out2), .out3(decoder_2_out3),
    .out4(decoder_2_out4), .out5(decoder_2_out5), .out6(decoder_2_out6), .out7(decoder_2_out7), .sel(A));  // open: en
  Decoder #(.select(3), .disabled(0)) decoder_3 (
    .out0(decoder_3_out0), .out1(decoder_3_out1), .out2(decoder_3_out2), .out3(decoder_3_out3),
    .out4(decoder_3_out4), .out5(decoder_3_out5), .out6(decoder_3_out6), .out7(decoder_3_out7), .sel(B));  // open: en
  not not_1 (not_1_out, 1'b0);
  assign controlled_buffer_17_out = not_1_out ? PbA : 16'bz;  // Controlled_Buffer controlled_buffer_17
  assign controlled_buffer_18_out = not_2_out ? PbB : 16'bz;  // Controlled_Buffer controlled_buffer_18
  not not_2 (not_2_out, AXB);
  Register #(.width(16)) AR (.D(Rb), .en(1'b0), .Q(AR_q), .clk(CLK), .clr(RST));
  ExactlyOne xor_1[15:0] (
    .out(xor_1_out), .in1(controlled_buffer_17_out), .in3(bit_extender_1_out), .in4(controlled_buffer_18_out));
  assign controlled_buffer_17_out = 1'b0 ? {16{1'b0}} : 16'bz;  // Controlled_Buffer controlled_buffer_19
  assign controlled_buffer_18_out = AXB ? {16{1'b0}} : 16'bz;  // Controlled_Buffer controlled_buffer_20
  ExactlyOne xor_2[15:0] (
    .out(xor_2_out), .in0(bit_extender_1_out), .in1(controlled_buffer_18_out), .in3(bit_extender_2_out));
  assign bit_extender_1_out = {{15{AIB}}, AIB};  // Bit_Extender bit_extender_1
  assign bit_extender_2_out = {{15{AIA}}, AIA};  // Bit_Extender bit_extender_2
  assign bit_extender_3_out = {{15{AIA}}, AIA};  // Bit_Extender bit_extender_3
  Pull_Resistor pull_resistor_1 (.node(Rb));
  Multiplexer #(.width(16)) multiplexer_1 (.in0(Rb), .in1(AR_q), .out(Ab), .sel(WM));  // open: en
  not not_3 (not_3_out, RM);
  assign Db = not_3_out ? Rb : 16'bz;  // Controlled_Buffer controlled_buffer_21
  Adder #(.width(16)) adder_1 (.a(xor_1_out), .b(xor_2_out), .out(adder_1_out), .cin(Cin), .cout(adder_1_cout));
  ExactlyOne xor_3[15:0] (.out(xor_3_out), .in1(xor_1_out), .in3(16'h8000), .in4(xor_2_out));
  Adder #(.width(16)) adder_2 (.a(xor_3_out), .b(xor_4_out), .cin(Cin), .cout(SCout));  // open: out
  ExactlyOne xor_4[15:0] (.out(xor_4_out), .in0(16'h8000), .in1(xor_2_out), .in3(16'h8000));
  assign xor_5_out = xor_1_out ^ xor_2_out;  // XOR_Gate xor_5, 16 bits wide
  // OR_Gate #(.width(16)) or_1: pin names not known; wires that end beside it: xor_1_out, xor_2_out, or_1_p3
  assign xor_6_out = or_1_p3 ^ bit_extender_3_out;  // XOR_Gate xor_6, 16 bits wide
  ROM #(.addrWidth(16), .dataWidth(16)) rom_1 (.addr(Ab), .data(rom_1_data), .sel(1'b1));
  RAM #(.addrWidth(16), .dataWidth(16)) ram_1 (
    .addr(Ab), .data(ram_1_data), .sel(1'b1), .clk(CLK), .ld(and_2_p2), .clr(RST));
  Comparator #(.width(16), .mode("unsigned")) comparator_1 (
    .a(Ab), .b({16{1'b1}}), .lt(comparator_1_lt));  // open: gt, eq
  assign Rb = AADD ? adder_1_out : 16'bz;  // Controlled_Buffer controlled_buffer_22
  assign Cout = AADD ? adder_1_cout : 1'bz;  // Controlled_Buffer controlled_buffer_23
  Pull_Resistor pull_resistor_2 (.node(Cout));
  assign Rb = AXOR ? xor_5_out : 16'bz;  // Controlled_Buffer controlled_buffer_24
  assign Rb = AOR ? xor_6_out : 16'bz;  // Controlled_Buffer controlled_buffer_25
  assign Rb = ASHL ? {xor_1_out[14:0], Cin} : 16'bz;  // Controlled_Buffer controlled_buffer_26
  assign Cout = ASHL ? xor_1_out[15] : 1'bz;  // Controlled_Buffer controlled_buffer_27
  assign Rb = ASHR ? {Cin, xor_1_out[15:1]} : 16'bz;  // Controlled_Buffer controlled_buffer_28
  assign Cout = ASHR ? xor_1_out[0] : 1'bz;  // Controlled_Buffer controlled_buffer_29
  assign Db = and_1_out ? rom_1_data : 16'bz;  // Controlled_Buffer controlled_buffer_30
  assign ram_1_data = WM ? Db : 16'bz;  // Controlled_Buffer controlled_buffer_31
  assign Db = and_2_p2 ? ram_1_data : 16'bz;  // Controlled_Buffer controlled_buffer_32
  and and_1 (and_1_out, RM, comparator_1_lt, RM);
  // AND_Gate and_2: pin names not known; wires that end beside it: comparator_1_lt, and_2_p2
  Register #(.width(10), .trigger("falling")) u_PS (.D({not_4_out, 1'b1}), .Q(PS), .clk(CLK), .clr(RST));  // open: en
  and and_3 (and_3_out, ~IA[0], ~IA[1], IA[2]);  // AND_Gate
  and and_4 (and_4_out, ~IB[0], ~IB[1], IB[2]);  // AND_Gate
  nand nand_1 (nand_1_out, IX[0], IX[1], IX[2]);
  not not_4 (not_4_out[1], PS[0]);
  Demultiplexer #(.disabled(0)) demultiplexer_1 (
    .out0(demultiplexer_1_out0), .out1(demultiplexer_1_out1), .in(PS[8]), .sel(not_5_out));  // open: en
  not not_5 (not_5_out, demultiplexer_2_out0);
  Demultiplexer #(.disabled(0)) demultiplexer_2 (
    .out0(demultiplexer_2_out0), .out1(demultiplexer_2_out1), .in(multiplexer_2_out), .sel(not_6_out));  // open: en
  not not_6 (not_6_out, IY);
  Multiplexer #(.disabled(0), .enable("true")) multiplexer_2 (
    .in0(and_3_out), .in1(and_4_out), .out(multiplexer_2_out), .sel(IY), .en(nand_1_out));
  // OR_Gate or_2: pin names not known; wires that end beside it: PS[0], PS[1], PS[1], PS[9], or_2_p5
  // OR_Gate or_3: pin names not known; wires that end beside it: or_2_p5, or_3_p2, not_4_out[2]
  or or_4 (or_3_p2, PS[5], demultiplexer_1_out1, demultiplexer_10_out1, PS[5]);
  nand nand_2 (nand_2_out, IA[0], IA[1], IA[2]);
  nand nand_3 (nand_3_out, IB[0], IB[1], IB[2]);
  or or_5 (or_5_out, 1'b0, 1'b0, 1'b0);
  // OR_Gate or_6: pin names not known; wires that end beside it: 1'b0, 1'b0, 1'b0, INC
  // AND_Gate and_5: pin names not known; wires that end beside it: 1'b0, 1'b0, 1'b0, and_5_p4
  and and_6 (and_6_out, 1'b0, nor_1_out);
  Demultiplexer #(.disabled(0)) demultiplexer_3 (
    .out0(demultiplexer_3_out0), .out1(demultiplexer_3_out1), .in(and_6_out), .sel(IY));  // open: en
  nor nor_1 (nor_1_out, 1'b0, 1'b0, 1'b0);
  // AND_Gate and_7: pin names not known; wires that end beside it: 1'b0, 1'b0, 1'b0, 1'b1, and_7_p5, and_7_p6
  // AND_Gate and_8: pin names not known; wires that end beside it: 1'b0, 1'b0, and_7_p6, and_7_p5
  Demultiplexer #(.disabled(0)) demultiplexer_4 (
    .out0(not_4_out[3]), .out1(demultiplexer_4_out1), .in(PS[2]), .sel(nand_2_out));
  Demultiplexer #(.disabled(0)) demultiplexer_5 (
    .out0(not_4_out[5]), .out1(demultiplexer_5_out1), .in(or_7_out), .sel(nor_2_p2));  // open: en
  or or_7 (or_7_out, demultiplexer_6_out1, PS[4]);
  or or_8 (R6, or_5_out, INC);
  // OR_Gate or_9: pin names not known; wires that end beside it: 1'b0, demultiplexer_3_out0, Si0
  or or_10 (R4, 1'b0, 1'b0, 1'b0);
  or or_11 (RM, INC, or_5_out, and_5_p4);
  or or_12 (WR, and_7_p5, and_7_p6);
  // OR_Gate or_13: pin names not known; wires that end beside it: demultiplexer_4_out1, PS[3], or_13_p3
  Demultiplexer #(.disabled(0)) demultiplexer_6 (
    .out0(not_4_out[4]), .out1(demultiplexer_6_out1), .in(or_13_p3), .sel(nand_3_out));
  Demultiplexer #(.disabled(0)) demultiplexer_7 (
    .out0(demultiplexer_7_out0), .out1(demultiplexer_7_out1), .in(demultiplexer_5_out1), .sel(and_9_p2));
  Demultiplexer #(.disabled(0)) demultiplexer_8 (
    .out0(demultiplexer_8_out0), .out1(demultiplexer_8_out1), .in(PS[7]), .sel(IOp[5]));  // open: en
  // NOR_Gate nor_2: pin names not known; wires that end beside it: demultiplexer_2_out1, nor_2_p2, 1'b0, IOp[5]
  // AND_Gate and_9: pin names not known; wires that end beside it: nand_1_out, and_9_p2, IOp[5]
  // OR_Gate or_14: pin names not known; wires that end beside it: 1'b0, demultiplexer_3_out1, Si1
  Demultiplexer #(.disabled(0)) demultiplexer_9 (
    .out0(not_4_out[6]), .out1(demultiplexer_9_out1), .in(PS[5]), .sel(1'b0), .en(demultiplexer_7_out0));
  // OR_Gate or_15: pin names not known; wires that end beside it: demultiplexer_7_out1, demultiplexer_8_out0, not_4_out[8]
  Demultiplexer #(.disabled(0)) demultiplexer_10 (
    .out0(demultiplexer_10_out0), .out1(demultiplexer_10_out1), .in(demultiplexer_8_out1), .sel(not_5_out));
  Multiplexer #(.width(3), .disabled(0)) multiplexer_3 (
    .in0(IA), .in1(IB), .out(multiplexer_3_out), .sel(IY));  // open: en
  or or_16 (not_4_out[7], demultiplexer_9_out1, PS[6], demultiplexer_7_out0);
  // OR_Gate or_17: pin names not known; wires that end beside it: demultiplexer_10_out0, demultiplexer_1_out0, not_4_out[9]
  or or_18 (or_18_out[2], R6, R4);
  assign A = or_18_out[2] ? {or_18_out[2], R6, 1'b0} : 3'bz;  // Controlled_Buffer controlled_buffer_33
  Pull_Resistor pull_resistor_3 (.node(A));
  assign A = 1'b0 ? IX : 3'bz;  // Controlled_Buffer controlled_buffer_34
  assign A = 1'b1 ? IA : 3'bz;  // Controlled_Buffer controlled_buffer_35
  assign B = or_18_out[2] ? {or_18_out[2], R6, 1'b0} : 3'bz;  // Controlled_Buffer controlled_buffer_36
  assign B = 1'b0 ? multiplexer_3_out : 3'bz;  // Controlled_Buffer controlled_buffer_37
  Pull_Resistor pull_resistor_4 (.node(B));
  assign B = 1'b1 ? IB : 3'bz;  // Controlled_Buffer controlled_buffer_38
  assign D = or_18_out[2] ? {or_18_out[2], R6, 1'b0} : 3'bz;  // Controlled_Buffer controlled_buffer_39
  Pull_Resistor pull_resistor_5 (.node(D));
  assign D = 1'b0 ? IA : 3'bz;  // Controlled_Buffer controlled_buffer_40
  assign D = 1'b1 ? IA : 3'bz;  // Controlled_Buffer controlled_buffer_41
  not not_7 (not_7_out, 1'b0);
  Multiplexer #(.width(3)) multiplexer_4 (
    .in0(3'b111), .in1(3'b111), .out(multiplexer_4_out), .sel(not_7_out));  // open: en
  // OR_Gate or_19: pin names not known; wires that end beside it: 1'b0, or_19_p2, 1'b0
  Multiplexer #(.width(3)) multiplexer_5 (
    .in0(3'b100), .in1(3'b111), .out(multiplexer_5_out), .sel(not_7_out));  // open: en
  // OR_Gate or_20: pin names not known; wires that end beside it: 1'b0, or_20_p2, 1'b0
  Register #(.width(1)) Y (.D(1'b0), .en(1'b0), .Q(IY), .clk(CLK), .clr(RST));
  Register #(.width(3)) X (.D(3'b111), .en(1'b0), .Q(IX), .clk(CLK), .clr(RST));
  Register #(.width(3)) u_B (.D(multiplexer_4_out), .en(or_19_p2), .Q(IB), .clk(CLK), .clr(RST));
  Register #(.width(3)) u_A (.D(multiplexer_5_out), .en(or_20_p2), .Q(IA), .clk(CLK), .clr(RST));
  Register #(.width(6)) Opcode (.D(6'b100110), .en(1'b0), .Q(IOp), .clk(CLK), .clr(RST));
  Decoder #(.select(3), .disabled(0), .enable("true")) decoder_4 (
    .out0(decoder_4_out0), .out1(decoder_4_out1), .out2(decoder_4_out2), .out3(AIA), .out4(decoder_4_out4),
    .out5(AXOR), .out6(ASHL), .out7(ASHR), .sel(3'b001), .en(and_10_p2));
  // AND_Gate and_10: pin names not known; wires that end beside it: 1'b0, and_10_p2, and_10_p3
  not not_8 (and_10_p3, 1'b0);
  and and_11 (AXB, 1'b0, 1'b0);
  or or_21 (or_21_out, decoder_4_out1, decoder_4_out2);
  not not_9 (not_9_out, decoder_4_out0);
  // XOR_Gate xor_7: pin names not known; wires that end beside it: not_9_out, AXB, xor_7_p3
  or or_22 (AADD, 1'b0, decoder_4_out0, or_21_out);
  // OR_Gate or_23: pin names not known; wires that end beside it: or_21_out, AIA, AIB
  // OR_Gate or_24: pin names not known; wires that end beside it: or_21_out, AIA, decoder_4_out4, AOR
  Multiplexer #(.disabled(0), .enable("true")) multiplexer_6 (
    .in0(xor_7_p3), .in1(1'b0), .out(Cin), .sel(1'b0), .en(1'b0));

  // Notes on the sheet:
  //   PbA
  //   PbB
  //   Rb
  //   Db
  //   Ab
  //   Registers file
  //   Arithmetic And Logic unit
  //   Memory
  //   SHL
  //   SHR
  //   contents of rom_1 (hex, n*v repeats v):
  //   0 0 cccc 52425*0 ffee
  //   CU
  //   Boot 0
  //   Boot 1
  //   Load 0
  //   Load 1
  //   Load 2
  //   Push
  //   Jsr
  //   Addr
  //   Act
  //   Pop
  //   MOV
  //   LEA
  //   CMP
  //   State machine / Instruction decoder
  //   Boot 0
  //   Boot 1
  //   Load 0
  //   Load 1
  //   Load 2
  //   Push
  //   Jsr
  //   Addr
  //   Act
  //   Pop
  //   Is Jsr
  //   Instruction unpacker
  //   ALU decoder
  //   PASS
  //   ADD
  //   SUB
  //   CMP
  //   AND
  //   OR
  //   XOR
  //   SHL
  //   SHR
  //   CC
  //   MATH1
  //   MOV
  //   LEA
endmodule
