// Logisim project testing.circ as structural Verilog: 1 circuit, main circuit main
module main (
);

  wire Clock_out, comparator_1_eq, comparator_1_lt, comparator_2_eq, comparator_2_gt, or_1_out, Reset_out;
  wire [4:0] bit_extender_1_out, bit_extender_2_out;
  wire [31:0] Accumulator_q, adder_1_out, Limit_q, Mask_q, pull_resistor_1_node, pull_resistor_2_node,
       shifter_1_out, shifter_2_out, Value_q;

  Button Reset (.out(Reset_out));
  Clock Clock (.out(Clock_out));
  Register #(.width(32)) Accumulator (.D(adder_1_out), .en(1'b1), .Q(Accumulator_q), .clk(Clock_out), .clr(Reset_out));
  Register #(.width(32)) Value (.D(shifter_1_out), .en(1'b1), .Q(Value_q), .clk(Clock_out), .clr(Reset_out));
  Register #(.width(32)) Mask (.D(shifter_2_out), .en(1'b1), .Q(Mask_q), .clk(Clock_out), .clr(Reset_out));
  Counter #(.width(32), .max('hffffffff)) Limit (
    .load(1'b1), .count(1'b0), .Q(Limit_q), .clk(Clock_out), .clr(Reset_out));  // open: D, carry
  Pull_Resistor pull_resistor_1 (.node(pull_resistor_1_node));
  assign pull_resistor_1_node = 1'b1 ? Accumulator_q : 32'bz;  // Controlled_Buffer controlled_buffer_1
  Pull_Resistor pull_resistor_2 (.node(pull_resistor_2_node));
  assign pull_resistor_2_node = Mask_q[0] ? Value_q : 32'bz;  // Controlled_Buffer controlled_buffer_2
  Adder #(.width(32)) adder_1 (
    .a(pull_resistor_1_node), .b(pull_resistor_2_node), .out(adder_1_out));  // open: cin, cout
  Shifter #(.width(32)) shifter_1 (.in(Value_q), .\dist (bit_extender_1_out), .out(shifter_1_out));
  assign bit_extender_1_out = {{4{1'b0}}, 1'b1};  // Bit_Extender bit_extender_1
  Shifter #(.width(32), .shift("lr")) shifter_2 (.in(Mask_q), .\dist (bit_extender_2_out), .out(shifter_2_out));
  assign bit_extender_2_out = {{4{1'b0}}, 1'b1};  // Bit_Extender bit_extender_2
  Comparator #(.width(32), .mode("unsigned")) comparator_1 (
    .a(Mask_q), .b({32{1'b0}}), .eq(comparator_1_eq), .lt(comparator_1_lt));  // open: gt
  or or_1 (or_1_out, comparator_1_eq, comparator_1_lt, comparator_2_gt, comparator_2_eq);
  Comparator #(.width(32), .mode("unsigned")) comparator_2 (
    .a(Limit_q), .b({32{1'b0}}), .gt(comparator_2_gt), .eq(comparator_2_eq));  // open: lt
  LED Done (.in(or_1_out));
endmodule
